# Fritzing sketch UZA80 (saved by Fritzing 0.3.16b)
breadboards: 1

parts:
  RLY2 = FRM1-1C1 Relay
  Exhaust_Close_Relay = NPN-Transistor [package="TO92 [THT]"]
  Exhaust_Open_Relay = NPN-Transistor [package="TO92 [THT]"]
  D1 = Rectifier Diode [package="300 mil [THT]"]
  D1_2 = Rectifier Diode [package="300 mil [THT]"]
  R1 = Resistor [resistance=2.2k package=THT]
  R1_2 = Resistor [resistance=2.2k package=THT]
  Arduino1 = Arduino
  J1 = screw terminal, 8 pins
  IC1 = IC, DIP package, 14 pins [chip_label=LM1815 spacing=300mil]
  R3 = Resistor [resistance=5.6k package=THT]
  R4 = Resistor [resistance=150k package=THT]
  R5 = Resistor [resistance=18k package=THT]
  C1 = Ceramic Capacitor [package=THT]
  C2 = Electrolytic Capacitor [package=THT]
  R6 = Resistor [resistance=1M package=THT]
  RLY1 = FRM1-1C1 Relay
  R1_3 = Resistor [resistance=2.2k package=THT]
  Reverse_Lockout_Solenoid = NPN-Transistor [package="TO92 [THT]"]
  Speedo_Output = NPN-Transistor [package="TO92 [THT]"]
  R1_4 = Resistor [resistance=2.2k package=THT]
  C1_2 = Ceramic Capacitor [package=THT]
  D1_3 = Rectifier Diode [package="300 mil [THT]"]
  J2 = screw terminal, 4 pins

nets:
  N1: RLY2.connector0, RLY2.connector4, D1.cathode, D1_2.cathode, Arduino1.VIN, RLY1.connector0, RLY1.connector4, D1_3.cathode, J2.pin2, J2.pin3
  N2: RLY2.connector1, Exhaust_Close_Relay.C, Exhaust_Open_Relay.C, Arduino1.GND, IC1.pin2, IC1.pin9, IC1.pin11, C1.pin_0, C2.-, R6.Pin_1, RLY1.connector1, Reverse_Lockout_Solenoid.C, C1_2.pin_0, J2.pin4
  N3: RLY2.connector2, J1.pin5
  N4: RLY2.connector3, Exhaust_Close_Relay.E, D1.anode
  N5: Exhaust_Close_Relay.B, R1_3.Pin_1
  N6: Exhaust_Open_Relay.E, D1_2.anode, RLY1.connector3
  N7: Exhaust_Open_Relay.B, R1.Pin_1
  N8: R1.Pin_0, Arduino1.D2
  N9: R1_2.Pin_0, Arduino1.D11
  N10: R1_2.Pin_1, Reverse_Lockout_Solenoid.B
  N11: Arduino1.D12, IC1.pin12, R3.Pin_1
  N12: Arduino1.D10, R1_4.Pin_0
  N13: Arduino1.D4, J1.pin6
  N14: Arduino1.D3, R1_3.Pin_0
  N15: Arduino1.+5V, IC1.pin8, R3.Pin_0, R4.Pin_0, Speedo_Output.C
  N16: J1.pin2, Speedo_Output.E
  N17: J1.pin3, Reverse_Lockout_Solenoid.E, D1_3.anode
  N18: J1.pin4, RLY1.connector2
  N19: J1.pin7, R5.Pin_0
  N20: IC1.pin3, R5.Pin_1, C1.pin_1
  N21: IC1.pin7, C2.+, R6.Pin_0
  N22: IC1.pin14, R4.Pin_1, C1_2.pin_1
  N23: Speedo_Output.B, R1_4.Pin_1
